// Logisim project CPU_MEM.circ as structural Verilog
module CPU_MEM_1 (
  input  S,
  input  E,
  output Q
);

  wire nand_1_out, nand_2_out, nand_4_out;

  nand nand_1 (nand_1_out, S, E);
  nand nand_2 (nand_2_out, nand_1_out, E);
  nand nand_3 (Q, nand_1_out, nand_4_out);
  nand nand_4 (nand_4_out, Q, nand_2_out);

  // Notes on the sheet:
  //   1 bit memory cell
endmodule

module CPU_MEM_8 (
  input  [7:0] in_1,
  input  in_2,
  output [7:0] out_3
);

  CPU_MEM_1 cpu_mem_1_1 (.S(in_1[0]), .E(in_2), .Q(out_3[0]));
  CPU_MEM_1 cpu_mem_1_2 (.S(in_1[1]), .E(in_2), .Q(out_3[1]));
  CPU_MEM_1 cpu_mem_1_3 (.S(in_1[2]), .E(in_2), .Q(out_3[2]));
  CPU_MEM_1 cpu_mem_1_4 (.S(in_1[3]), .E(in_2), .Q(out_3[3]));
  CPU_MEM_1 cpu_mem_1_5 (.S(in_1[4]), .E(in_2), .Q(out_3[4]));
  CPU_MEM_1 cpu_mem_1_6 (.S(in_1[5]), .E(in_2), .Q(out_3[5]));
  CPU_MEM_1 cpu_mem_1_7 (.S(in_1[6]), .E(in_2), .Q(out_3[6]));
  CPU_MEM_1 cpu_mem_1_8 (.S(in_1[7]), .E(in_2), .Q(out_3[7]));
endmodule
